// Logisim project nand2tetris.circ as structural Verilog
module NotGate (
  input  inp,
  output outp
);

  nand nand_1 (outp, inp, inp);
endmodule

module AndGate (
  input  a,
  input  b,
  output outp
);

  wire nand_1_out;

  nand nand_1 (nand_1_out, a, b);
  NotGate notgate_1 (.inp(nand_1_out), .outp(outp));
endmodule

module OrGate (
  input  a,
  input  b,
  output outp
);

  wire notgate_1_outp, notgate_2_outp;

  NotGate notgate_1 (.inp(a), .outp(notgate_1_outp));
  NotGate notgate_2 (.inp(b), .outp(notgate_2_outp));
  nand nand_1 (outp, notgate_1_outp, notgate_2_outp);
endmodule

module XorGate (
  input  in_1,
  input  in_2,
  output out_3
);

  wire nand_1_out, orgate_1_outp;

  nand nand_1 (nand_1_out, in_1, in_2);
  OrGate orgate_1 (.a(in_2), .b(in_1), .outp(orgate_1_outp));
  AndGate andgate_1 (.a(nand_1_out), .b(orgate_1_outp), .outp(out_3));
endmodule

module Mux (
  input  a,
  input  b,
  input  sel,
  output outp
);

  wire andgate_1_outp, andgate_2_outp, notgate_1_outp;

  NotGate notgate_1 (.inp(sel), .outp(notgate_1_outp));
  AndGate andgate_1 (.a(notgate_1_outp), .b(a), .outp(andgate_1_outp));
  AndGate andgate_2 (.a(b), .b(sel), .outp(andgate_2_outp));
  OrGate orgate_1 (.a(andgate_2_outp), .b(andgate_1_outp), .outp(outp));
endmodule

module DMux (
  input  in_1,
  input  in_2,
  output out_3,
  output out_4
);

  wire notgate_1_outp;

  NotGate notgate_1 (.inp(in_2), .outp(notgate_1_outp));
  AndGate andgate_1 (.a(notgate_1_outp), .b(in_1), .outp(out_3));
  AndGate andgate_2 (.a(in_1), .b(in_2), .outp(out_4));
endmodule

module Not16 (
  input  [15:0] in16,
  output [15:0] out16
);

  NotGate notgate_1 (.inp(in16[0]), .outp(out16[0]));
  NotGate notgate_2 (.inp(in16[1]), .outp(out16[1]));
  NotGate notgate_3 (.inp(in16[2]), .outp(out16[2]));
  NotGate notgate_4 (.inp(in16[3]), .outp(out16[3]));
  NotGate notgate_5 (.inp(in16[4]), .outp(out16[4]));
  NotGate notgate_6 (.inp(in16[5]), .outp(out16[5]));
  NotGate notgate_7 (.inp(in16[6]), .outp(out16[6]));
  NotGate notgate_8 (.inp(in16[7]), .outp(out16[7]));
  NotGate notgate_9 (.inp(in16[8]), .outp(out16[8]));
  NotGate notgate_10 (.inp(in16[9]), .outp(out16[9]));
  NotGate notgate_11 (.inp(in16[10]), .outp(out16[10]));
  NotGate notgate_12 (.inp(in16[11]), .outp(out16[11]));
  NotGate notgate_13 (.inp(in16[12]), .outp(out16[12]));
  NotGate notgate_14 (.inp(in16[13]), .outp(out16[13]));
  NotGate notgate_15 (.inp(in16[14]), .outp(out16[14]));
  NotGate notgate_16 (.inp(in16[15]), .outp(out16[15]));
endmodule

module And16 (
  input  [15:0] b16,
  input  [15:0] a16,
  output [15:0] out16
);

  AndGate andgate_1 (.a(a16[0]), .b(b16[0]), .outp(out16[0]));
  AndGate andgate_2 (.a(a16[1]), .b(b16[1]), .outp(out16[1]));
  AndGate andgate_3 (.a(a16[2]), .b(b16[2]), .outp(out16[2]));
  AndGate andgate_4 (.a(a16[3]), .b(b16[3]), .outp(out16[3]));
  AndGate andgate_5 (.a(a16[4]), .b(b16[4]), .outp(out16[4]));
  AndGate andgate_6 (.a(a16[5]), .b(b16[5]), .outp(out16[5]));
  AndGate andgate_7 (.a(a16[6]), .b(b16[6]), .outp(out16[6]));
  AndGate andgate_8 (.a(a16[7]), .b(b16[7]), .outp(out16[7]));
  AndGate andgate_9 (.a(a16[8]), .b(b16[8]), .outp(out16[8]));
  AndGate andgate_10 (.a(a16[9]), .b(b16[9]), .outp(out16[9]));
  AndGate andgate_11 (.a(a16[10]), .b(b16[10]), .outp(out16[10]));
  AndGate andgate_12 (.a(a16[11]), .b(b16[11]), .outp(out16[11]));
  AndGate andgate_13 (.a(a16[12]), .b(b16[12]), .outp(out16[12]));
  AndGate andgate_14 (.a(a16[13]), .b(b16[13]), .outp(out16[13]));
  AndGate andgate_15 (.a(a16[14]), .b(b16[14]), .outp(out16[14]));
  AndGate andgate_16 (.a(a16[15]), .b(b16[15]), .outp(out16[15]));
endmodule

module Or16 (
  input  [15:0] b16,
  input  [15:0] a16,
  output [15:0] out16
);

  OrGate orgate_1 (.a(b16[0]), .b(a16[0]), .outp(out16[0]));
  OrGate orgate_2 (.a(b16[1]), .b(a16[1]), .outp(out16[1]));
  OrGate orgate_3 (.a(b16[2]), .b(a16[2]), .outp(out16[2]));
  OrGate orgate_4 (.a(b16[3]), .b(a16[3]), .outp(out16[3]));
  OrGate orgate_5 (.a(b16[4]), .b(a16[4]), .outp(out16[4]));
  OrGate orgate_6 (.a(b16[5]), .b(a16[5]), .outp(out16[5]));
  OrGate orgate_7 (.a(b16[6]), .b(a16[6]), .outp(out16[6]));
  OrGate orgate_8 (.a(b16[7]), .b(a16[7]), .outp(out16[7]));
  OrGate orgate_9 (.a(b16[8]), .b(a16[8]), .outp(out16[8]));
  OrGate orgate_10 (.a(b16[9]), .b(a16[9]), .outp(out16[9]));
  OrGate orgate_11 (.a(b16[10]), .b(a16[10]), .outp(out16[10]));
  OrGate orgate_12 (.a(b16[11]), .b(a16[11]), .outp(out16[11]));
  OrGate orgate_13 (.a(b16[12]), .b(a16[12]), .outp(out16[12]));
  OrGate orgate_14 (.a(b16[13]), .b(a16[13]), .outp(out16[13]));
  OrGate orgate_15 (.a(b16[14]), .b(a16[14]), .outp(out16[14]));
  OrGate orgate_16 (.a(b16[15]), .b(a16[15]), .outp(out16[15]));
endmodule

module Mux16 (
  input  sel,
  input  [15:0] b16,
  input  [15:0] a16,
  output [15:0] out16
);

  Mux mux_1 (.a(a16[0]), .b(b16[0]), .sel(sel), .outp(out16[0]));
  Mux mux_2 (.a(a16[1]), .b(b16[1]), .sel(sel), .outp(out16[1]));
  Mux mux_3 (.a(a16[2]), .b(b16[2]), .sel(sel), .outp(out16[2]));
  Mux mux_4 (.a(a16[3]), .b(b16[3]), .sel(sel), .outp(out16[3]));
  Mux mux_5 (.a(a16[4]), .b(b16[4]), .sel(sel), .outp(out16[4]));
  Mux mux_6 (.a(a16[5]), .b(b16[5]), .sel(sel), .outp(out16[5]));
  Mux mux_7 (.a(a16[6]), .b(b16[6]), .sel(sel), .outp(out16[6]));
  Mux mux_8 (.a(a16[7]), .b(b16[7]), .sel(sel), .outp(out16[7]));
  Mux mux_9 (.a(a16[8]), .b(b16[8]), .sel(sel), .outp(out16[8]));
  Mux mux_10 (.a(a16[9]), .b(b16[9]), .sel(sel), .outp(out16[9]));
  Mux mux_11 (.a(a16[10]), .b(b16[10]), .sel(sel), .outp(out16[10]));
  Mux mux_12 (.a(a16[11]), .b(b16[11]), .sel(sel), .outp(out16[11]));
  Mux mux_13 (.a(a16[12]), .b(b16[12]), .sel(sel), .outp(out16[12]));
  Mux mux_14 (.a(a16[13]), .b(b16[13]), .sel(sel), .outp(out16[13]));
  Mux mux_15 (.a(a16[14]), .b(b16[14]), .sel(sel), .outp(out16[14]));
  Mux mux_16 (.a(a16[15]), .b(b16[15]), .sel(sel), .outp(out16[15]));
endmodule

module Or8Way (
  input  [7:0] in8,
  output outp
);

  wire orgate_1_outp, orgate_2_outp, orgate_3_outp, orgate_4_outp, orgate_5_outp, orgate_6_outp;

  OrGate orgate_1 (.a(in8[1]), .b(in8[0]), .outp(orgate_1_outp));
  OrGate orgate_2 (.a(in8[2]), .b(orgate_1_outp), .outp(orgate_2_outp));
  OrGate orgate_3 (.a(in8[3]), .b(orgate_2_outp), .outp(orgate_3_outp));
  OrGate orgate_4 (.a(in8[4]), .b(orgate_3_outp), .outp(orgate_4_outp));
  OrGate orgate_5 (.a(in8[5]), .b(orgate_4_outp), .outp(orgate_5_outp));
  OrGate orgate_6 (.a(in8[6]), .b(orgate_5_outp), .outp(orgate_6_outp));
  OrGate orgate_7 (.a(in8[7]), .b(orgate_6_outp), .outp(outp));
endmodule

module Mux4Way16 (
  input  [15:0] a16,
  input  [15:0] b16,
  input  [15:0] c16,
  input  [15:0] d16,
  input  [1:0] sel2,
  output [15:0] out16
);

  wire [15:0] mux16_1_out16, mux16_2_out16;

  Mux16 mux16_1 (.b16(b16), .a16(a16), .sel(sel2[0]), .out16(mux16_1_out16));
  Mux16 mux16_2 (.b16(d16), .a16(c16), .sel(sel2[0]), .out16(mux16_2_out16));
  Mux16 mux16_3 (.b16(mux16_2_out16), .a16(mux16_1_out16), .sel(sel2[1]), .out16(out16));
endmodule

module Mux8Way16 (
  input  [15:0] a16,
  input  [15:0] b16,
  input  [15:0] c16,
  input  [15:0] d16,
  input  [15:0] e16,
  input  [15:0] f16,
  input  [15:0] g16,
  input  [15:0] h16,
  input  [2:0] sel3,
  output [15:0] out16
);

  wire [15:0] mux4way16_1_out16, mux4way16_2_out16;

  Mux4Way16 mux4way16_1 (.a16(a16), .b16(b16), .c16(c16), .d16(d16), .sel2(sel3[1:0]), .out16(mux4way16_1_out16));
  Mux4Way16 mux4way16_2 (.a16(e16), .b16(f16), .c16(g16), .d16(h16), .sel2(sel3[1:0]), .out16(mux4way16_2_out16));
  Mux16 mux16_1 (.b16(mux4way16_2_out16), .a16(mux4way16_1_out16), .sel(sel3[2]), .out16(out16));
endmodule

module DMux4Way (
  input  inp,
  input  [1:0] sel2,
  output a,
  output b,
  output c,
  output d
);

  wire dmux_1_out_3, dmux_1_out_4;

  DMux dmux_1 (.in_1(inp), .in_2(sel2[1]), .out_3(dmux_1_out_3), .out_4(dmux_1_out_4));
  DMux dmux_2 (.in_1(dmux_1_out_3), .in_2(sel2[0]), .out_3(a), .out_4(b));
  DMux dmux_3 (.in_1(dmux_1_out_4), .in_2(sel2[0]), .out_3(c), .out_4(d));
endmodule

module DMux8Way (
  input  inp,
  input  [2:0] sel3,
  output a,
  output b,
  output c,
  output d,
  output e,
  output f,
  output g,
  output h
);

  wire dmux_1_out_3, dmux_1_out_4;

  DMux dmux_1 (.in_1(inp), .in_2(sel3[2]), .out_3(dmux_1_out_3), .out_4(dmux_1_out_4));
  DMux4Way dmux4way_1 (.inp(dmux_1_out_3), .sel2(sel3[1:0]), .a(a), .b(b), .c(c), .d(d));
  DMux4Way dmux4way_2 (.inp(dmux_1_out_4), .sel2(sel3[1:0]), .a(e), .b(f), .c(g), .d(h));
endmodule

module FullAdder (
  input  a,
  input  b,
  input  c,
  output sum,
  output carry
);

  wire halfadder_1_carry, halfadder_1_sum, halfadder_2_carry;

  HalfAdder halfadder_1 (.a(a), .b(b), .sum(halfadder_1_sum), .carry(halfadder_1_carry));
  HalfAdder halfadder_2 (.a(halfadder_1_sum), .b(c), .sum(sum), .carry(halfadder_2_carry));
  OrGate orgate_1 (.a(halfadder_1_carry), .b(halfadder_2_carry), .outp(carry));
endmodule

module HalfAdder (
  input  a,
  input  b,
  output sum,
  output carry
);

  XorGate xorgate_1 (.in_1(b), .in_2(a), .out_3(sum));
  AndGate andgate_1 (.a(a), .b(b), .outp(carry));
endmodule

module Add16 (
  input  [15:0] a16,
  input  [15:0] b16,
  output [15:0] out16
);

  wire fulladder_1_carry, fulladder_2_carry, fulladder_3_carry, fulladder_4_carry, fulladder_5_carry,
       fulladder_6_carry, fulladder_7_carry, fulladder_8_carry, fulladder_9_carry, fulladder_10_carry,
       fulladder_11_carry, fulladder_12_carry, fulladder_13_carry, fulladder_14_carry, halfadder_1_carry;

  HalfAdder halfadder_1 (.a(a16[0]), .b(b16[0]), .sum(out16[0]), .carry(halfadder_1_carry));
  FullAdder fulladder_1 (.a(a16[1]), .b(halfadder_1_carry), .c(b16[1]), .sum(out16[1]), .carry(fulladder_1_carry));
  FullAdder fulladder_2 (.a(a16[2]), .b(fulladder_1_carry), .c(b16[2]), .sum(out16[2]), .carry(fulladder_2_carry));
  FullAdder fulladder_3 (.a(a16[3]), .b(fulladder_2_carry), .c(b16[3]), .sum(out16[3]), .carry(fulladder_3_carry));
  FullAdder fulladder_4 (.a(a16[4]), .b(fulladder_3_carry), .c(b16[4]), .sum(out16[4]), .carry(fulladder_4_carry));
  FullAdder fulladder_5 (.a(a16[5]), .b(fulladder_4_carry), .c(b16[5]), .sum(out16[5]), .carry(fulladder_5_carry));
  FullAdder fulladder_6 (.a(a16[6]), .b(fulladder_5_carry), .c(b16[6]), .sum(out16[6]), .carry(fulladder_6_carry));
  FullAdder fulladder_7 (.a(a16[7]), .b(fulladder_6_carry), .c(b16[7]), .sum(out16[7]), .carry(fulladder_7_carry));
  FullAdder fulladder_8 (.a(a16[8]), .b(fulladder_7_carry), .c(b16[8]), .sum(out16[8]), .carry(fulladder_8_carry));
  FullAdder fulladder_9 (.a(a16[9]), .b(fulladder_8_carry), .c(b16[9]), .sum(out16[9]), .carry(fulladder_9_carry));
  FullAdder fulladder_10 (.a(a16[10]), .b(fulladder_9_carry), .c(b16[10]), .sum(out16[10]), .carry(fulladder_10_carry));
  FullAdder fulladder_11 (
    .a(a16[11]), .b(fulladder_10_carry), .c(b16[11]), .sum(out16[11]), .carry(fulladder_11_carry));
  FullAdder fulladder_12 (
    .a(a16[12]), .b(fulladder_11_carry), .c(b16[12]), .sum(out16[12]), .carry(fulladder_12_carry));
  FullAdder fulladder_13 (
    .a(a16[13]), .b(fulladder_12_carry), .c(b16[13]), .sum(out16[13]), .carry(fulladder_13_carry));
  FullAdder fulladder_14 (
    .a(a16[14]), .b(fulladder_13_carry), .c(b16[14]), .sum(out16[14]), .carry(fulladder_14_carry));
  FullAdder fulladder_15 (.a(a16[15]), .b(fulladder_14_carry), .c(b16[15]), .sum(out16[15]));  // open: carry
endmodule

module Inc16 (
  input  [15:0] in16,
  output [15:0] out16
);

  wire halfadder_1_carry, halfadder_2_carry, halfadder_3_carry, halfadder_4_carry, halfadder_5_carry,
       halfadder_6_carry, halfadder_7_carry, halfadder_8_carry, halfadder_9_carry, halfadder_10_carry,
       halfadder_11_carry, halfadder_12_carry, halfadder_13_carry, halfadder_14_carry, halfadder_15_carry;

  HalfAdder halfadder_1 (.a(1'b1), .b(in16[0]), .sum(out16[0]), .carry(halfadder_1_carry));
  HalfAdder halfadder_2 (.a(halfadder_1_carry), .b(in16[1]), .sum(out16[1]), .carry(halfadder_2_carry));
  HalfAdder halfadder_3 (.a(halfadder_2_carry), .b(in16[2]), .sum(out16[2]), .carry(halfadder_3_carry));
  HalfAdder halfadder_4 (.a(halfadder_3_carry), .b(in16[3]), .sum(out16[3]), .carry(halfadder_4_carry));
  HalfAdder halfadder_5 (.a(halfadder_4_carry), .b(in16[4]), .sum(out16[4]), .carry(halfadder_5_carry));
  HalfAdder halfadder_6 (.a(halfadder_5_carry), .b(in16[5]), .sum(out16[5]), .carry(halfadder_6_carry));
  HalfAdder halfadder_7 (.a(halfadder_6_carry), .b(in16[6]), .sum(out16[6]), .carry(halfadder_7_carry));
  HalfAdder halfadder_8 (.a(halfadder_7_carry), .b(in16[7]), .sum(out16[7]), .carry(halfadder_8_carry));
  HalfAdder halfadder_9 (.a(halfadder_8_carry), .b(in16[8]), .sum(out16[8]), .carry(halfadder_9_carry));
  HalfAdder halfadder_10 (.a(halfadder_9_carry), .b(in16[9]), .sum(out16[9]), .carry(halfadder_10_carry));
  HalfAdder halfadder_11 (.a(halfadder_10_carry), .b(in16[10]), .sum(out16[10]), .carry(halfadder_11_carry));
  HalfAdder halfadder_12 (.a(halfadder_11_carry), .b(in16[11]), .sum(out16[11]), .carry(halfadder_12_carry));
  HalfAdder halfadder_13 (.a(halfadder_12_carry), .b(in16[12]), .sum(out16[12]), .carry(halfadder_13_carry));
  HalfAdder halfadder_14 (.a(halfadder_13_carry), .b(in16[13]), .sum(out16[13]), .carry(halfadder_14_carry));
  HalfAdder halfadder_15 (.a(halfadder_14_carry), .b(in16[14]), .sum(out16[14]), .carry(halfadder_15_carry));
  HalfAdder halfadder_16 (.a(halfadder_15_carry), .b(in16[15]), .sum(out16[15]));  // open: carry
endmodule

module ALU (
  input  zx,
  input  nx,
  input  zy,
  input  ny,
  input  f,
  input  no,
  input  [15:0] x16,
  input  [15:0] y16,
  output [15:0] out16,
  output zr,
  output ng
);

  wire or8way_1_outp, or8way_2_outp, orgate_1_outp;
  wire [15:0] add16_1_out16, and16_1_out16, mux16_1_out16, mux16_2_out16, mux16_3_out16, mux16_4_out16,
       mux16_5_out16, not16_1_out16, not16_2_out16, not16_3_out16;

  Mux16 mux16_1 (.b16({16{1'b0}}), .a16(x16), .sel(zx), .out16(mux16_1_out16));
  Mux16 mux16_2 (.b16({16{1'b0}}), .a16(y16), .sel(zy), .out16(mux16_2_out16));
  Not16 not16_1 (.in16(mux16_1_out16), .out16(not16_1_out16));
  Not16 not16_2 (.in16(mux16_2_out16), .out16(not16_2_out16));
  Mux16 mux16_3 (.b16(not16_1_out16), .a16(mux16_1_out16), .sel(nx), .out16(mux16_3_out16));
  Mux16 mux16_4 (.b16(not16_2_out16), .a16(mux16_2_out16), .sel(ny), .out16(mux16_4_out16));
  And16 and16_1 (.b16(mux16_4_out16), .a16(mux16_3_out16), .out16(and16_1_out16));
  Add16 add16_1 (.a16(mux16_3_out16), .b16(mux16_4_out16), .out16(add16_1_out16));
  Mux16 mux16_5 (.b16(add16_1_out16), .a16(and16_1_out16), .sel(f), .out16(mux16_5_out16));
  Not16 not16_3 (.in16(mux16_5_out16), .out16(not16_3_out16));
  Mux16 mux16_6 (.b16(not16_3_out16), .a16(mux16_5_out16), .sel(no), .out16({ng, out16[14:0]}));
  Or8Way or8way_1 (.in8(out16[7:0]), .outp(or8way_1_outp));
  Or8Way or8way_2 (.in8({ng, out16[14:8]}), .outp(or8way_2_outp));
  OrGate orgate_1 (.a(or8way_2_outp), .b(or8way_1_outp), .outp(orgate_1_outp));
  NotGate notgate_1 (.inp(orgate_1_outp), .outp(zr));

  assign out16[15] = ng;
endmodule

module Bit (
  input  load,
  input  inp,
  input  clk,
  output outp
);

  wire mux_1_outp;

  Mux mux_1 (.a(outp), .b(inp), .sel(load), .outp(mux_1_outp));
  D_Flip_Flop d_ff_1 (.D(mux_1_outp), .clk(clk), .Q(outp));  // open: Qn, preset, reset
endmodule

module Register16 (
  input  clk,
  input  load,
  input  [15:0] in16,
  output [15:0] out16
);

  Bit bit_1 (.inp(in16[0]), .load(load), .clk(clk), .outp(out16[0]));
  Bit bit_2 (.inp(in16[1]), .load(load), .clk(clk), .outp(out16[1]));
  Bit bit_3 (.inp(in16[2]), .load(load), .clk(clk), .outp(out16[2]));
  Bit bit_4 (.inp(in16[3]), .load(load), .clk(clk), .outp(out16[3]));
  Bit bit_5 (.inp(in16[4]), .load(load), .clk(clk), .outp(out16[4]));
  Bit bit_6 (.inp(in16[5]), .load(load), .clk(clk), .outp(out16[5]));
  Bit bit_7 (.inp(in16[6]), .load(load), .clk(clk), .outp(out16[6]));
  Bit bit_8 (.inp(in16[7]), .load(load), .clk(clk), .outp(out16[7]));
  Bit bit_9 (.inp(in16[8]), .load(load), .clk(clk), .outp(out16[8]));
  Bit bit_10 (.inp(in16[9]), .load(load), .clk(clk), .outp(out16[9]));
  Bit bit_11 (.inp(in16[10]), .load(load), .clk(clk), .outp(out16[10]));
  Bit bit_12 (.inp(in16[11]), .load(load), .clk(clk), .outp(out16[11]));
  Bit bit_13 (.inp(in16[12]), .load(load), .clk(clk), .outp(out16[12]));
  Bit bit_14 (.inp(in16[13]), .load(load), .clk(clk), .outp(out16[13]));
  Bit bit_15 (.inp(in16[14]), .load(load), .clk(clk), .outp(out16[14]));
  Bit bit_16 (.inp(in16[15]), .load(load), .clk(clk), .outp(out16[15]));
endmodule

module RAM8 (
  input  load,
  input  clk,
  input  [15:0] in16,
  input  [2:0] address,
  output [15:0] out16
);

  wire dmux8way_1_a, dmux8way_1_b, dmux8way_1_c, dmux8way_1_d, dmux8way_1_e, dmux8way_1_f, dmux8way_1_g,
       dmux8way_1_h;
  wire [15:0] register16_1_out16, register16_2_out16, register16_3_out16, register16_4_out16,
       register16_5_out16, register16_6_out16, register16_7_out16, register16_8_out16;

  DMux8Way dmux8way_1 (
    .inp(load), .sel3(address), .a(dmux8way_1_a), .b(dmux8way_1_b), .c(dmux8way_1_c), .d(dmux8way_1_d),
    .e(dmux8way_1_e), .f(dmux8way_1_f), .g(dmux8way_1_g), .h(dmux8way_1_h));
  Register16 register16_1 (.in16(in16), .clk(clk), .load(dmux8way_1_a), .out16(register16_1_out16));
  Register16 register16_2 (.in16(in16), .clk(clk), .load(dmux8way_1_b), .out16(register16_2_out16));
  Register16 register16_3 (.in16(in16), .clk(clk), .load(dmux8way_1_c), .out16(register16_3_out16));
  Register16 register16_4 (.in16(in16), .clk(clk), .load(dmux8way_1_d), .out16(register16_4_out16));
  Register16 register16_5 (.in16(in16), .clk(clk), .load(dmux8way_1_e), .out16(register16_5_out16));
  Register16 register16_6 (.in16(in16), .clk(clk), .load(dmux8way_1_f), .out16(register16_6_out16));
  Register16 register16_7 (.in16(in16), .clk(clk), .load(dmux8way_1_g), .out16(register16_7_out16));
  Register16 register16_8 (.in16(in16), .clk(clk), .load(dmux8way_1_h), .out16(register16_8_out16));
  Mux8Way16 mux8way16_1 (
    .sel3(address), .a16(register16_1_out16), .b16(register16_2_out16), .c16(register16_3_out16),
    .d16(register16_4_out16), .e16(register16_5_out16), .f16(register16_6_out16), .g16(register16_7_out16),
    .h16(register16_8_out16), .out16(out16));
endmodule

module RAM8BuiltIn (
  input  [2:0] address,
  input  load,
  input  clk,
  input  [15:0] in16,
  output [15:0] out16
);

  RAM #(.addrWidth(3), .dataWidth(16), .enables("line")) ram_1 (
    .addr(address), .we(load), .clk(clk), .din(in16), .dout(out16));
endmodule

module RAM64 (
  input  load,
  input  clk,
  input  [15:0] in16,
  input  [5:0] address,
  output [15:0] out16
);

  wire dmux8way_1_a, dmux8way_1_b, dmux8way_1_c, dmux8way_1_d, dmux8way_1_e, dmux8way_1_f, dmux8way_1_g,
       dmux8way_1_h;
  wire [15:0] ram8builtin_1_out16, ram8builtin_2_out16, ram8builtin_3_out16, ram8builtin_4_out16,
       ram8builtin_5_out16, ram8builtin_6_out16, ram8builtin_7_out16, ram8builtin_8_out16;

  DMux8Way dmux8way_1 (
    .inp(load), .sel3(address[2:0]), .a(dmux8way_1_a), .b(dmux8way_1_b), .c(dmux8way_1_c), .d(dmux8way_1_d),
    .e(dmux8way_1_e), .f(dmux8way_1_f), .g(dmux8way_1_g), .h(dmux8way_1_h));
  RAM8BuiltIn ram8builtin_1 (
    .load(dmux8way_1_a), .address(address[5:3]), .in16(in16), .clk(clk), .out16(ram8builtin_1_out16));
  RAM8BuiltIn ram8builtin_2 (
    .load(dmux8way_1_b), .address(address[5:3]), .in16(in16), .clk(clk), .out16(ram8builtin_2_out16));
  RAM8BuiltIn ram8builtin_3 (
    .load(dmux8way_1_c), .address(address[5:3]), .in16(in16), .clk(clk), .out16(ram8builtin_3_out16));
  RAM8BuiltIn ram8builtin_4 (
    .load(dmux8way_1_d), .address(address[5:3]), .in16(in16), .clk(clk), .out16(ram8builtin_4_out16));
  RAM8BuiltIn ram8builtin_5 (
    .load(dmux8way_1_e), .address(address[5:3]), .in16(in16), .clk(clk), .out16(ram8builtin_5_out16));
  RAM8BuiltIn ram8builtin_6 (
    .load(dmux8way_1_f), .address(address[5:3]), .in16(in16), .clk(clk), .out16(ram8builtin_6_out16));
  RAM8BuiltIn ram8builtin_7 (
    .load(dmux8way_1_g), .address(address[5:3]), .in16(in16), .clk(clk), .out16(ram8builtin_7_out16));
  RAM8BuiltIn ram8builtin_8 (
    .load(dmux8way_1_h), .address(address[5:3]), .in16(in16), .clk(clk), .out16(ram8builtin_8_out16));
  Mux8Way16 mux8way16_1 (
    .sel3(address[2:0]), .a16(ram8builtin_1_out16), .b16(ram8builtin_2_out16), .c16(ram8builtin_3_out16),
    .d16(ram8builtin_4_out16), .e16(ram8builtin_5_out16), .f16(ram8builtin_6_out16),
    .g16(ram8builtin_7_out16), .h16(ram8builtin_8_out16), .out16(out16));
endmodule

module RAM64BuiltIn (
  input  [5:0] address,
  input  load,
  input  clk,
  input  [15:0] in16,
  output [15:0] out16
);

  RAM #(.addrWidth(6), .dataWidth(16), .enables("line")) ram_1 (
    .addr(address), .we(load), .clk(clk), .din(in16), .dout(out16));
endmodule

module RAM512 (
  input  load,
  input  clk,
  input  [15:0] in16,
  input  [8:0] address,
  output [15:0] out16
);

  wire dmux8way_1_a, dmux8way_1_b, dmux8way_1_c, dmux8way_1_d, dmux8way_1_e, dmux8way_1_f, dmux8way_1_g,
       dmux8way_1_h;
  wire [15:0] ram64builtin_1_out16, ram64builtin_2_out16, ram64builtin_3_out16, ram64builtin_4_out16,
       ram64builtin_5_out16, ram64builtin_6_out16, ram64builtin_7_out16, ram64builtin_8_out16;

  DMux8Way dmux8way_1 (
    .inp(load), .sel3(address[2:0]), .a(dmux8way_1_a), .b(dmux8way_1_b), .c(dmux8way_1_c), .d(dmux8way_1_d),
    .e(dmux8way_1_e), .f(dmux8way_1_f), .g(dmux8way_1_g), .h(dmux8way_1_h));
  RAM64BuiltIn ram64builtin_1 (
    .load(dmux8way_1_a), .address(address[8:3]), .in16(in16), .clk(clk), .out16(ram64builtin_1_out16));
  RAM64BuiltIn ram64builtin_2 (
    .load(dmux8way_1_b), .address(address[8:3]), .in16(in16), .clk(clk), .out16(ram64builtin_2_out16));
  RAM64BuiltIn ram64builtin_3 (
    .load(dmux8way_1_c), .address(address[8:3]), .in16(in16), .clk(clk), .out16(ram64builtin_3_out16));
  RAM64BuiltIn ram64builtin_4 (
    .load(dmux8way_1_d), .address(address[8:3]), .in16(in16), .clk(clk), .out16(ram64builtin_4_out16));
  RAM64BuiltIn ram64builtin_5 (
    .load(dmux8way_1_e), .address(address[8:3]), .in16(in16), .clk(clk), .out16(ram64builtin_5_out16));
  RAM64BuiltIn ram64builtin_6 (
    .load(dmux8way_1_f), .address(address[8:3]), .in16(in16), .clk(clk), .out16(ram64builtin_6_out16));
  RAM64BuiltIn ram64builtin_7 (
    .load(dmux8way_1_g), .address(address[8:3]), .in16(in16), .clk(clk), .out16(ram64builtin_7_out16));
  RAM64BuiltIn ram64builtin_8 (
    .load(dmux8way_1_h), .address(address[8:3]), .in16(in16), .clk(clk), .out16(ram64builtin_8_out16));
  Mux8Way16 mux8way16_1 (
    .sel3(address[2:0]), .a16(ram64builtin_1_out16), .b16(ram64builtin_2_out16), .c16(ram64builtin_3_out16),
    .d16(ram64builtin_4_out16), .e16(ram64builtin_5_out16), .f16(ram64builtin_6_out16),
    .g16(ram64builtin_7_out16), .h16(ram64builtin_8_out16), .out16(out16));
endmodule

module RAM512BuiltIn (
  input  [8:0] address,
  input  load,
  input  clk,
  input  [15:0] in16,
  output [15:0] out16
);

  RAM #(.addrWidth(9), .dataWidth(16), .enables("line")) ram_1 (
    .addr(address), .we(load), .clk(clk), .din(in16), .dout(out16));
endmodule

module RAM4K (
  input  load,
  input  clk,
  input  [15:0] in16,
  input  [11:0] address,
  output [15:0] out16
);

  wire dmux8way_1_a, dmux8way_1_b, dmux8way_1_c, dmux8way_1_d, dmux8way_1_e, dmux8way_1_f, dmux8way_1_g,
       dmux8way_1_h;
  wire [15:0] ram512builtin_1_out16, ram512builtin_2_out16, ram512builtin_3_out16, ram512builtin_4_out16,
       ram512builtin_5_out16, ram512builtin_6_out16, ram512builtin_7_out16, ram512builtin_8_out16;

  DMux8Way dmux8way_1 (
    .inp(load), .sel3(address[2:0]), .a(dmux8way_1_a), .b(dmux8way_1_b), .c(dmux8way_1_c), .d(dmux8way_1_d),
    .e(dmux8way_1_e), .f(dmux8way_1_f), .g(dmux8way_1_g), .h(dmux8way_1_h));
  RAM512BuiltIn ram512builtin_1 (
    .load(dmux8way_1_a), .address(address[11:3]), .in16(in16), .clk(clk), .out16(ram512builtin_1_out16));
  RAM512BuiltIn ram512builtin_2 (
    .load(dmux8way_1_b), .address(address[11:3]), .in16(in16), .clk(clk), .out16(ram512builtin_2_out16));
  RAM512BuiltIn ram512builtin_3 (
    .load(dmux8way_1_c), .address(address[11:3]), .in16(in16), .clk(clk), .out16(ram512builtin_3_out16));
  RAM512BuiltIn ram512builtin_4 (
    .load(dmux8way_1_d), .address(address[11:3]), .in16(in16), .clk(clk), .out16(ram512builtin_4_out16));
  RAM512BuiltIn ram512builtin_5 (
    .load(dmux8way_1_e), .address(address[11:3]), .in16(in16), .clk(clk), .out16(ram512builtin_5_out16));
  RAM512BuiltIn ram512builtin_6 (
    .load(dmux8way_1_f), .address(address[11:3]), .in16(in16), .clk(clk), .out16(ram512builtin_6_out16));
  RAM512BuiltIn ram512builtin_7 (
    .load(dmux8way_1_g), .address(address[11:3]), .in16(in16), .clk(clk), .out16(ram512builtin_7_out16));
  RAM512BuiltIn ram512builtin_8 (
    .load(dmux8way_1_h), .address(address[11:3]), .in16(in16), .clk(clk), .out16(ram512builtin_8_out16));
  Mux8Way16 mux8way16_1 (
    .sel3(address[2:0]), .a16(ram512builtin_1_out16), .b16(ram512builtin_2_out16),
    .c16(ram512builtin_3_out16), .d16(ram512builtin_4_out16), .e16(ram512builtin_5_out16),
    .f16(ram512builtin_6_out16), .g16(ram512builtin_7_out16), .h16(ram512builtin_8_out16), .out16(out16));
endmodule

module RAM4KBuiltIn (
  input  [11:0] address,
  input  load,
  input  clk,
  input  [15:0] in16,
  output [15:0] out16
);

  RAM #(.addrWidth(12), .dataWidth(16), .enables("line")) ram_1 (
    .addr(address), .we(load), .clk(clk), .din(in16), .dout(out16));
endmodule

module RAM16K (
  input  load,
  input  clk,
  input  [15:0] in16,
  input  [13:0] address,
  output [15:0] out16
);

  wire dmux4way_1_a, dmux4way_1_b, dmux4way_1_c, dmux4way_1_d;
  wire [15:0] ram4kbuiltin_1_out16, ram4kbuiltin_2_out16, ram4kbuiltin_3_out16, ram4kbuiltin_4_out16;

  DMux4Way dmux4way_1 (
    .inp(load), .sel2(address[1:0]), .a(dmux4way_1_a), .b(dmux4way_1_b), .c(dmux4way_1_c), .d(dmux4way_1_d));
  RAM4KBuiltIn ram4kbuiltin_1 (
    .load(dmux4way_1_a), .address(address[13:2]), .in16(in16), .clk(clk), .out16(ram4kbuiltin_1_out16));
  RAM4KBuiltIn ram4kbuiltin_2 (
    .load(dmux4way_1_b), .address(address[13:2]), .in16(in16), .clk(clk), .out16(ram4kbuiltin_2_out16));
  RAM4KBuiltIn ram4kbuiltin_3 (
    .load(dmux4way_1_c), .address(address[13:2]), .in16(in16), .clk(clk), .out16(ram4kbuiltin_3_out16));
  RAM4KBuiltIn ram4kbuiltin_4 (
    .load(dmux4way_1_d), .address(address[13:2]), .in16(in16), .clk(clk), .out16(ram4kbuiltin_4_out16));
  Mux4Way16 mux4way16_1 (
    .a16(ram4kbuiltin_1_out16), .b16(ram4kbuiltin_2_out16), .c16(ram4kbuiltin_3_out16),
    .d16(ram4kbuiltin_4_out16), .sel2(address[1:0]), .out16(out16));
endmodule

module PC (
  input  inc,
  input  load,
  input  reset,
  input  clk,
  input  [15:0] in16,
  output [15:0] out16
);

  wire [15:0] inc16_1_out16, mux16_1_out16, mux16_2_out16, mux16_3_out16;

  Mux16 mux16_1 (.b16(inc16_1_out16), .a16(out16), .sel(inc), .out16(mux16_1_out16));
  Mux16 mux16_2 (.b16(in16), .a16(mux16_1_out16), .sel(load), .out16(mux16_2_out16));
  Mux16 mux16_3 (.b16({16{1'b0}}), .a16(mux16_2_out16), .sel(reset), .out16(mux16_3_out16));
  Register16 register16_1 (.in16(mux16_3_out16), .clk(clk), .load(1'b1), .out16(out16));
  Inc16 inc16_1 (.in16(out16), .out16(inc16_1_out16));
endmodule

module RAM16KBuiltIn (
  input  [13:0] address,
  input  load,
  input  clk,
  input  [15:0] in16,
  output [15:0] out16
);

  RAM #(.addrWidth(14), .dataWidth(16), .enables("line")) ram_1 (
    .addr(address), .we(load), .clk(clk), .din(in16), .dout(out16));
endmodule

module Memory (
  input  load,
  input  clk,
  input  [15:0] in16,
  input  [14:0] address15,
  output [15:0] out16
);

  wire dmux_1_out_3, dmux_1_out_4, dmux_2_out_3, dmux_2_out_4, dmux_3_out_3, dmux_3_out_4;
  wire [15:0] mux16_1_out16, mux16_2_out16, ram4kbuiltin_1_out16, ram4kbuiltin_2_out16,
       ram16kbuiltin_1_out16, register16_1_out16;

  DMux dmux_1 (.in_1(load), .in_2(address15[14]), .out_3(dmux_1_out_3), .out_4(dmux_1_out_4));
  DMux dmux_2 (.in_1(dmux_1_out_4), .in_2(address15[12]), .out_3(dmux_2_out_3), .out_4(dmux_2_out_4));
  DMux dmux_3 (.in_1(dmux_2_out_3), .in_2(address15[13]), .out_3(dmux_3_out_3), .out_4(dmux_3_out_4));
  RAM16KBuiltIn ram16kbuiltin_1 (
    .load(dmux_1_out_3), .address(address15[13:0]), .in16(in16), .clk(clk), .out16(ram16kbuiltin_1_out16));
  RAM4KBuiltIn ram4kbuiltin_1 (
    .load(dmux_3_out_3), .address(address15[11:0]), .in16(in16), .clk(clk), .out16(ram4kbuiltin_1_out16));
  RAM4KBuiltIn ram4kbuiltin_2 (
    .load(dmux_2_out_4), .address(address15[11:0]), .in16(in16), .clk(clk), .out16(ram4kbuiltin_2_out16));
  Register16 register16_1 (.in16(in16), .clk(clk), .load(dmux_3_out_4), .out16(register16_1_out16));
  Mux16 mux16_1 (.b16(ram4kbuiltin_2_out16), .a16(ram4kbuiltin_1_out16), .sel(address15[12]), .out16(mux16_1_out16));
  Mux16 mux16_2 (.b16(register16_1_out16), .a16(mux16_1_out16), .sel(address15[13]), .out16(mux16_2_out16));
  Mux16 mux16_3 (.b16(mux16_2_out16), .a16(ram16kbuiltin_1_out16), .sel(address15[14]), .out16(out16));

  // Notes on the sheet:
  //   RAM
  //   Screen1
  //   Screen2
  //   Keyboard
endmodule

module DualPortRAM8K (
  input  clk,
  input  [15:0] in16,
  input  load,
  input  [12:0] a_address,
  input  [12:0] b_address,
  output [15:0] a_out,
  output [15:0] b_out
);

  wire and_1_out, clk_read, clk_write;
  wire [12:0] multiplexer_1_out;

  and and_1 (and_1_out, load, clk_write);
  Multiplexer #(.width(13)) multiplexer_1 (.in0(a_address), .in1(b_address), .out(multiplexer_1_out), .sel(clk_read));
  Counter #(.max('h1), .width(1)) counter_1 (.Q(clk_read), .clk(clk));  // open: load, D, count, carry, up, clr
  not not_1 (clk_write, clk_read);
  RAM #(.addrWidth(13), .asyncread("true"), .dataWidth(16)) ram_1 (
    .addr(a_address), .we(and_1_out), .clk(clk), .din(in16), .dout(a_out));  // open: oe
  RAM #(.addrWidth(13), .asyncread("true"), .dataWidth(16)) ram_2 (
    .addr(multiplexer_1_out), .we(and_1_out), .clk(clk), .din(in16), .dout(b_out));  // open: oe

  // Notes on the sheet:
  //   out values will be valid at the system clk frequency
  //   has to be 2x the system clk
endmodule

module VideoCard512x256 (
  input  clk,
  input  [15:0] inM,
  output outValue,
  output [12:0] addressM,
  output [8:0] x,
  output [7:0] y
);

  wire and_1_out, and_2_out, and_3_out, and_4_out, register_1_q;
  wire [3:0] \bit ;

  Register #(.width(1)) register_1 (.D(and_1_out), .en(clk), .clk(clk), .Q(register_1_q));  // open: clr
  Counter #(.max('h1fff), .width(13)) counter_1 (
    .load(and_3_out), .D({13{1'b0}}), .count(and_4_out), .Q(addressM), .clk(clk));  // open: carry, up, clr
  Counter #(.max('h1ff), .width(9)) counter_2 (
    .load(and_1_out), .D({9{1'b0}}), .count(clk), .Q(x), .clk(clk));  // open: carry, up, clr
  Counter counter_3 (
    .load(and_2_out), .D({8{1'b0}}), .count(register_1_q), .Q(y), .clk(register_1_q));  // open: carry, up, clr
  and and_1 (and_1_out, x[0], x[1], x[2], x[3], x[4], x[5], x[6], x[7], x[8]);
  and and_2 (and_2_out, y[0], y[1], y[2], y[3], y[4], y[5], y[6], y[7]);
  and and_3 (and_3_out, addressM[0], addressM[1], addressM[2], addressM[3], addressM[4], addressM[5], addressM[6], addressM[7], addressM[8], addressM[9], addressM[10], addressM[11], addressM[12]);
  Multiplexer #(.select(4)) multiplexer_1 (
    .in0(inM[0]), .in1(inM[1]), .in2(inM[2]), .in3(inM[3]), .in4(inM[4]), .in5(inM[5]), .in6(inM[6]),
    .in7(inM[7]), .in8(inM[8]), .in9(inM[9]), .in10(inM[10]), .in11(inM[11]), .in12(inM[12]), .in13(inM[13]),
    .in14(inM[14]), .in15(inM[15]), .out(outValue), .sel(\bit ));
  Counter #(.max('hf), .width(4)) counter_4 (
    .load(and_4_out), .D(4'b0000), .Q(\bit ), .clk(clk));  // open: count, carry, up, clr
  and and_4 (and_4_out, \bit [0], \bit [1], \bit [2], \bit [3]);

  // Notes on the sheet:
  //   Counting X
  //   Counting Y
  //   Counting the RAM address
  //   y++ after x passes 255
  //   == 8191
  //   Counting the bits in the 16-bit registers
  //   == 15
endmodule

module VideoCard128x128 (
  input  clk,
  input  [15:0] inM,
  output outValue,
  output [12:0] addressM,
  output [3:0] out_5,
  output [6:0] x,
  output [6:0] y
);

  wire and_1_out, and_2_out, and_3_out, and_4_out, register_1_q;

  Register #(.width(1)) register_1 (.D(and_1_out), .en(clk), .clk(clk), .Q(register_1_q));  // open: clr
  Counter #(.max('h1fff), .width(13)) counter_1 (
    .load(and_3_out), .D({13{1'b0}}), .count(and_4_out), .Q(addressM), .clk(clk));  // open: carry, up, clr
  Counter #(.max('h7f), .width(7)) counter_2 (
    .load(and_1_out), .D({7{1'b0}}), .count(clk), .Q(x), .clk(clk));  // open: carry, up, clr
  Counter #(.max('h7f), .width(7)) counter_3 (
    .load(and_2_out), .D({7{1'b0}}), .count(register_1_q), .Q(y), .clk(register_1_q));  // open: carry, up, clr
  and and_1 (and_1_out, x[0], x[1], x[2], x[3], x[4], x[5], x[6]);
  and and_2 (and_2_out, y[0], y[1], y[2], y[3], y[4], y[5], y[6]);
  Multiplexer #(.select(4)) multiplexer_1 (
    .in0(inM[0]), .in1(inM[1]), .in2(inM[2]), .in3(inM[3]), .in4(inM[4]), .in5(inM[5]), .in6(inM[6]),
    .in7(inM[7]), .in8(inM[8]), .in9(inM[9]), .in10(inM[10]), .in11(inM[11]), .in12(inM[12]), .in13(inM[13]),
    .in14(inM[14]), .in15(inM[15]), .out(outValue), .sel(out_5));
  and and_3 (and_3_out, addressM[0], addressM[1], addressM[2], addressM[3], addressM[4], addressM[5], addressM[6], addressM[7], addressM[8], addressM[9]);
  Counter #(.max('hf), .width(4)) counter_4 (
    .load(and_4_out), .D(4'b0000), .Q(out_5), .clk(clk));  // open: count, carry, up, clr
  and and_4 (and_4_out, out_5[0], out_5[1], out_5[2], out_5[3]);

  // Other names for the same wires on the sheet: bit[3:0] = out_5

  // Notes on the sheet:
  //   Counting X
  //   Counting Y
  //   Counting the RAM address
  //   y++ after x passes 127
  //   == 1023
  //   Counting the bits in the 16-bit registers
  //   == 15
endmodule

module VideoCard512x256Test (
  input  in_1,
  input  [15:0] in_2
);

  wire clk, rgb_video_1_p3;
  wire [2:2] rgb_video_1_p6;
  wire [7:0] rgb_video_1_p5;
  wire [8:0] rgb_video_1_p4;
  wire [12:0] videocard512x256_1_addressm;
  wire [15:0] ram_1_dout;

  Clock clock_1 (.out(clk));
  RAM #(.addrWidth(13), .dataWidth(16)) ram_1 (
    .addr(videocard512x256_1_addressm), .clk(clk), .dout(ram_1_dout));  // open: we, oe, din
  // RGB_Video #(.cursor("No Cursor"), .height(256), .width(256)) rgb_video_1: pin names not known; wires that end beside it: in_1, clk, rgb_video_1_p3, rgb_video_1_p4[7:0], rgb_video_1_p5, {3{rgb_video_1_p6[2]}}, ram_1_dout
  not not_1 (rgb_video_1_p3, rgb_video_1_p4[8]);
  VideoCard512x256 videocard512x256_1 (
    .clk(clk), .inM(in_2), .y(rgb_video_1_p5), .x(rgb_video_1_p4), .addressM(videocard512x256_1_addressm),
    .outValue(rgb_video_1_p6[2]));
  // RGB_Video #(.cursor("No Cursor"), .height(256), .width(256)) rgb_video_2: pin names not known; wires that end beside it: in_1, clk, rgb_video_1_p4[8], rgb_video_1_p4[7:0], rgb_video_1_p5, {3{rgb_video_1_p6[2]}}
endmodule

module VideoCard128x128Test (
  input  in_1,
  input  [15:0] in_2
);

  wire clk;
  wire [2:2] videocard128x128_1_outvalue;
  wire [6:0] videocard128x128_1_x, videocard128x128_1_y;
  wire [12:0] videocard128x128_1_addressm;
  wire [15:0] ram_1_dout;

  Clock clock_1 (.out(clk));
  RAM #(.addrWidth(13), .dataWidth(16)) ram_1 (
    .addr(videocard128x128_1_addressm), .clk(clk), .dout(ram_1_dout));  // open: we, oe, din
  VideoCard128x128 videocard128x128_1 (
    .clk(clk), .inM(in_2), .y(videocard128x128_1_y), .x(videocard128x128_1_x),
    .addressM(videocard128x128_1_addressm), .outValue(videocard128x128_1_outvalue[2]));  // open: out_5
  // RGB_Video rgb_video_1: pin names not known; wires that end beside it: in_1, clk, 1'b1, videocard128x128_1_x, videocard128x128_1_y, {3{videocard128x128_1_outvalue[2]}}
endmodule

module RegisterKbd (
  input  clk,
  input  [15:0] in16,
  input  load,
  output [15:0] out16
);

  wire and_1_out, clk_read, clk_write;

  and and_1 (and_1_out, load, clk_write);
  Counter #(.max('h1), .width(1)) counter_1 (.Q(clk_read), .clk(clk));  // open: load, D, count, carry, up, clr
  Register #(.width(16)) register_1 (.D(in16), .en(and_1_out), .clk(clk), .Q(out16));  // open: clr
  not not_1 (clk_write, clk_read);

  // Notes on the sheet:
  //   has to be 2x the system clock, this way in "one system cycle" write and read can happen 
  //   ie. the cpu can read the pressed key and the keyboard can set the pressed key at the same time/on the same cycle
endmodule

module MemoryWithIO (
  input  [15:0] in16,
  input  clk_2x,
  input  clk,
  input  load,
  input  [14:0] address15,
  input  [12:0] addressScreen,
  input  loadKbd,
  input  [15:0] inKbd,
  output [15:0] out16,
  output [15:0] outScreen
);

  wire demultiplexer_1_out0, demultiplexer_1_out1;
  wire [15:0] dualportram8k_1_a_out, multiplexer_1_out, ram16kbuiltin_1_out16, registerkbd_1_out16;

  Demultiplexer demultiplexer_1 (
    .out0(demultiplexer_1_out0), .out1(demultiplexer_1_out1), .in(load), .sel(address15[14]));
  RAM16KBuiltIn ram16kbuiltin_1 (
    .load(demultiplexer_1_out0), .address(address15[13:0]), .in16(in16), .clk(clk),
    .out16(ram16kbuiltin_1_out16));
  DualPortRAM8K dualportram8k_1 (
    .load(demultiplexer_1_out1), .a_address(address15[12:0]), .b_address(addressScreen), .clk(clk_2x),
    .in16(in16), .a_out(dualportram8k_1_a_out), .b_out(outScreen));
  RegisterKbd registerkbd_1 (.clk(clk_2x), .load(loadKbd), .in16(inKbd), .out16(registerkbd_1_out16));
  Multiplexer #(.width(16)) multiplexer_1 (
    .in0(dualportram8k_1_a_out), .in1(registerkbd_1_out16), .out(multiplexer_1_out), .sel(address15[13]));
  Multiplexer #(.width(16)) multiplexer_2 (
    .in0(ram16kbuiltin_1_out16), .in1(multiplexer_1_out), .out(out16), .sel(address15[14]));
endmodule
